// Logisim project control-logic.circ as structural Verilog: 1 circuit, main circuit control_logic
module control_logic (
  input  [31:0] Instruction,
  input  BrEq,
  input  BrLt,
  output PCSel,
  output RegWEn,
  output [2:0] ImmSel,
  output BrUn,
  output ASel,
  output BSel,
  output [3:0] ALUSel,
  output MemWEn,
  output [1:0] WBSel
);

  wire add1, addi, and1, and_1_out, and_2_out, and_3_out, and_4_out, andi, aupic, B, beq, bge, bgeu, blt,
       bltu, bne, decoder_2_out0, decoder_2_out1, decoder_2_out5, decoder_4_out5, I1, I2, jal, jalr, lb, lh,
       lui, lw, mul1, mulh1, mulhu1, not_1_out, not_2_out, or1, or_1_out, or_2_out, or_3_out, ori, R, S, sb,
       sh, sll1, slli, slt1, slti, sra1, srai, srl1, srli, sub1, sw, xor1, xori;
  wire [5:0] ROMInput;
  wire [15:14] rom_1_data;

  Decoder #(.select(5)) decoder_1 (
    .out0(I1), .out4(I2), .out5(aupic), .out8(S), .out12(R), .out13(lui), .out24(B), .out25(jalr),
    .out27(jal), .sel(Instruction[6:2]), .en(1'b1));  // open: out1, out2, out3, out6, out7, out9, out10, out11, out14, out15, out16, out17, out18, out19, out20, out21, out22, out23, out26, out28, out29, out30, out31
  ROM #(.addrWidth(6), .dataWidth(16)) rom_1 (
    .addr(ROMInput), .data({rom_1_data, WBSel, MemWEn, ALUSel, BSel, ASel, BrUn, ImmSel, RegWEn}));
  Decoder #(.select(3)) decoder_2 (
    .out0(decoder_2_out0), .out1(decoder_2_out1), .out2(slt1), .out3(mulhu1), .out4(xor1),
    .out5(decoder_2_out5), .out6(or1), .out7(and1), .sel(Instruction[14:12]), .en(R));
  Decoder #(.select(3)) decoder_3 (
    .out0(beq), .out1(bne), .out4(blt), .out5(bge), .out6(bltu), .out7(bgeu), .sel(Instruction[14:12]), .en(B));  // open: out2, out3
  Decoder #(.select(3)) decoder_4 (
    .out0(addi), .out1(slli), .out2(slti), .out4(xori), .out5(decoder_4_out5), .out6(ori), .out7(andi),
    .sel(Instruction[14:12]), .en(I2));  // open: out3
  Decoder #(.select(3)) decoder_5 (
    .out0(lb), .out1(lh), .out2(lw), .sel(Instruction[14:12]), .en(I1));  // open: out3, out4, out5, out6, out7
  Decoder #(.select(3)) decoder_6 (
    .out0(sb), .out1(sh), .out2(sw), .sel(Instruction[14:12]), .en(S));  // open: out3, out4, out5, out6, out7
  Decoder decoder_7 (.out0(sll1), .out1(mulh1), .sel(Instruction[25]), .en(decoder_2_out1));
  Decoder decoder_8 (.out0(srl1), .out1(sra1), .sel(Instruction[30]), .en(decoder_2_out5));
  Decoder decoder_9 (.out0(srli), .out1(srai), .sel(Instruction[30]), .en(decoder_4_out5));
  Decoder #(.select(2)) decoder_10 (
    .out0(add1), .out1(mul1), .out2(sub1), .sel({Instruction[30], Instruction[25]}), .en(decoder_2_out0));  // open: out3
  not not_1 (not_1_out, BrEq);
  or or_1 (or_1_out, blt, bltu);
  not not_2 (not_2_out, BrLt);
  or or_2 (or_2_out, bge, bgeu);
  and and_1 (and_1_out, BrEq, beq);
  and and_2 (and_2_out, not_1_out, bne);
  or or_3 (or_3_out, and_1_out, and_2_out, and_3_out, and_4_out);
  and and_3 (and_3_out, BrLt, or_1_out);
  and and_4 (and_4_out, not_2_out, or_2_out);
  or or_4 (PCSel, jal, jalr, or_3_out);
  Priority_Encoder #(.select_enc(6)) priority_encoder_1 (
    .in0(add1), .in1(mul1), .in2(sub1), .in3(sll1), .in4(mulh1), .in5(mulhu1), .in6(slt1), .in7(xor1),
    .in8(srl1), .in9(sra1), .in10(or1), .in11(and1), .in12(lb), .in13(lh), .in14(lw), .in15(addi),
    .in16(slli), .in17(slti), .in18(xori), .in19(srli), .in20(srai), .in21(ori), .in22(andi), .in23(sb),
    .in24(sh), .in25(sw), .in26(beq), .in27(bne), .in28(blt), .in29(bge), .in30(bltu), .in31(bgeu),
    .in32(aupic), .in33(lui), .in34(jal), .in35(jalr), .out(ROMInput));  // open: in36, in37, in38, in39, in40, in41, in42, in43, in44, in45, in46, in47, in48, in49, in50, in51, in52, in53, in54, in55, in56, in57, in58, in59, in60, in61, in62, in63, gs, en_out, en_in

  // Notes on the sheet:
  //   INPUTS to your circuit
  //   Connect ROM Input here ->
  //   contents of rom_1 (hex, n*v repeats v):
  //   1001 1401 1601 1081 1481 1581 1101 1201 1281 1681 1301 1381 2041 2041 2041 1041 10c1 1141 1241 12c1
  //   16c1 1341 13c1 842 842 842 4*64 74 74 1067 17e7 69 41
  //   ROM FOR CONTROL LOGIC
  //   DON'T CHANGE THE LOCATIONS OF THE INPUTS AND OUTPUTS!
  //   This is only if you choose to do the ROM option
  //   CONNECT
  //   WIRE
  //   TO
  //   USE
  //   ROM
  //   OUTPUT from your circuit
  //   Reminder: If using ROM, use combinational logic for PCSel
endmodule
