// Logisim project regfile.circ as structural Verilog: 1 circuit, main circuit regfile
module regfile (
  input  [4:0] ReadReg1,
  input  [4:0] ReadReg2,
  input  [4:0] WriteReg,
  input  [31:0] RegWriteData,
  input  RegWEn,
  input  clk,
  output [31:0] ra,
  output [31:0] sp,
  output [31:0] t0,
  output [31:0] t1,
  output [31:0] t2,
  output [31:0] s0,
  output [31:0] s1,
  output [31:0] a0,
  output [31:0] RegReadData1,
  output [31:0] RegReadData2
);

  wire x0WE, x1WE, x2WE, x3WE, x4WE, x5WE, x6WE, x7WE, x8WE, x9WE, x10WE, x11WE, x12WE, x13WE, x14WE, x15WE,
       x16WE, x17WE, x18WE, x19WE, x20WE, x21WE, x22WE, x23WE, x24WE, x25WE, x26WE, x27WE, x28WE, x29WE,
       x30WE, x31WE;
  wire [31:0] x0, x3, x4, x11, x12, x13, x14, x15, x16, x17, x18, x19, x20, x21, x22, x23, x24, x25, x26,
       x27, x28, x29, x30, x31;

  Decoder #(.select(5)) decoder_1 (
    .out0(x0WE), .out1(x1WE), .out2(x2WE), .out3(x3WE), .out4(x4WE), .out5(x5WE), .out6(x6WE), .out7(x7WE),
    .out8(x8WE), .out9(x9WE), .out10(x10WE), .out11(x11WE), .out12(x12WE), .out13(x13WE), .out14(x14WE),
    .out15(x15WE), .out16(x16WE), .out17(x17WE), .out18(x18WE), .out19(x19WE), .out20(x20WE), .out21(x21WE),
    .out22(x22WE), .out23(x23WE), .out24(x24WE), .out25(x25WE), .out26(x26WE), .out27(x27WE), .out28(x28WE),
    .out29(x29WE), .out30(x30WE), .out31(x31WE), .sel(WriteReg), .en(RegWEn));
  Register #(.width(32)) register_1 (.D({32{1'b0}}), .en(x0WE), .clk(clk), .Q(x0));  // open: clr
  Register #(.width(32)) register_2 (.D(RegWriteData), .en(x1WE), .clk(clk), .Q(ra));  // open: clr
  Register #(.width(32)) register_3 (.D(RegWriteData), .en(x2WE), .clk(clk), .Q(sp));  // open: clr
  Register #(.width(32)) register_4 (.D(RegWriteData), .en(x3WE), .clk(clk), .Q(x3));  // open: clr
  Register #(.width(32)) register_5 (.D(RegWriteData), .en(x16WE), .clk(clk), .Q(x16));  // open: clr
  Register #(.width(32)) register_6 (.D(RegWriteData), .en(x17WE), .clk(clk), .Q(x17));  // open: clr
  Register #(.width(32)) register_7 (.D(RegWriteData), .en(x18WE), .clk(clk), .Q(x18));  // open: clr
  Register #(.width(32)) register_8 (.D(RegWriteData), .en(x19WE), .clk(clk), .Q(x19));  // open: clr
  Register #(.width(32)) register_9 (.D(RegWriteData), .en(x4WE), .clk(clk), .Q(x4));  // open: clr
  Register #(.width(32)) register_10 (.D(RegWriteData), .en(x5WE), .clk(clk), .Q(t0));  // open: clr
  Register #(.width(32)) register_11 (.D(RegWriteData), .en(x6WE), .clk(clk), .Q(t1));  // open: clr
  Register #(.width(32)) register_12 (.D(RegWriteData), .en(x7WE), .clk(clk), .Q(t2));  // open: clr
  Register #(.width(32)) register_13 (.D(RegWriteData), .en(x20WE), .clk(clk), .Q(x20));  // open: clr
  Register #(.width(32)) register_14 (.D(RegWriteData), .en(x21WE), .clk(clk), .Q(x21));  // open: clr
  Register #(.width(32)) register_15 (.D(RegWriteData), .en(x22WE), .clk(clk), .Q(x22));  // open: clr
  Register #(.width(32)) register_16 (.D(RegWriteData), .en(x23WE), .clk(clk), .Q(x23));  // open: clr
  Register #(.width(32)) register_17 (.D(RegWriteData), .en(x8WE), .clk(clk), .Q(s0));  // open: clr
  Register #(.width(32)) register_18 (.D(RegWriteData), .en(x9WE), .clk(clk), .Q(s1));  // open: clr
  Register #(.width(32)) register_19 (.D(RegWriteData), .en(x10WE), .clk(clk), .Q(a0));  // open: clr
  Register #(.width(32)) register_20 (.D(RegWriteData), .en(x11WE), .clk(clk), .Q(x11));  // open: clr
  Register #(.width(32)) register_21 (.D(RegWriteData), .en(x24WE), .clk(clk), .Q(x24));  // open: clr
  Register #(.width(32)) register_22 (.D(RegWriteData), .en(x25WE), .clk(clk), .Q(x25));  // open: clr
  Register #(.width(32)) register_23 (.D(RegWriteData), .en(x26WE), .clk(clk), .Q(x26));  // open: clr
  Register #(.width(32)) register_24 (.D(RegWriteData), .en(x27WE), .clk(clk), .Q(x27));  // open: clr
  Register #(.width(32)) register_25 (.D(RegWriteData), .en(x12WE), .clk(clk), .Q(x12));  // open: clr
  Register #(.width(32)) register_26 (.D(RegWriteData), .en(x13WE), .clk(clk), .Q(x13));  // open: clr
  Register #(.width(32)) register_27 (.D(RegWriteData), .en(x14WE), .clk(clk), .Q(x14));  // open: clr
  Register #(.width(32)) register_28 (.D(RegWriteData), .en(x15WE), .clk(clk), .Q(x15));  // open: clr
  Register #(.width(32)) register_29 (.D(RegWriteData), .en(x28WE), .clk(clk), .Q(x28));  // open: clr
  Register #(.width(32)) register_30 (.D(RegWriteData), .en(x29WE), .clk(clk), .Q(x29));  // open: clr
  Register #(.width(32)) register_31 (.D(RegWriteData), .en(x30WE), .clk(clk), .Q(x30));  // open: clr
  Register #(.width(32)) register_32 (.D(RegWriteData), .en(x31WE), .clk(clk), .Q(x31));  // open: clr
  Multiplexer #(.select(5), .width(32)) multiplexer_1 (
    .in0(x0), .in1(ra), .in2(sp), .in3(x3), .in4(x4), .in5(t0), .in6(t1), .in7(t2), .in8(s0), .in9(s1),
    .in10(a0), .in11(x11), .in12(x12), .in13(x13), .in14(x14), .in15(x15), .in16(x16), .in17(x17),
    .in18(x18), .in19(x19), .in20(x20), .in21(x21), .in22(x22), .in23(x23), .in24(x24), .in25(x25),
    .in26(x26), .in27(x27), .in28(x28), .in29(x29), .in30(x30), .in31(x31), .out(RegReadData1), .sel(ReadReg1));
  Multiplexer #(.select(5), .width(32)) multiplexer_2 (
    .in0(x0), .in1(ra), .in2(sp), .in3(x3), .in4(x4), .in5(t0), .in6(t1), .in7(t2), .in8(s0), .in9(s1),
    .in10(a0), .in11(x11), .in12(x12), .in13(x13), .in14(x14), .in15(x15), .in16(x16), .in17(x17),
    .in18(x18), .in19(x19), .in20(x20), .in21(x21), .in22(x22), .in23(x23), .in24(x24), .in25(x25),
    .in26(x26), .in27(x27), .in28(x28), .in29(x29), .in30(x30), .in31(x31), .out(RegReadData2), .sel(ReadReg2));

  // Other names for the same wires on the sheet: x1[31:0] = ra; x2[31:0] = sp; x5[31:0] = t0; x6[31:0] = t1;
  //   x7[31:0] = t2; x8[31:0] = s0; x9[31:0] = s1; x10[31:0] = a0

  // Notes on the sheet:
  //   INPUTS to your circuit
  //   DON'T CHANGE THE LOCATIONS OF THE INPUTS AND OUTPUTS!
  //   These are DEBUG/TEST outputs from your circuit.
  //   OUTPUTS from your circuit
endmodule
